# Fritzing sketch ZonaDelSilencio (saved by Fritzing 0.8.7b)
breadboards: 1

parts:
  Emergency_Switch = Round Pushbutton
  Normal_Switch = Round Pushbutton
  R1 = Resistor [tolerance=±5% resistance=220 package=THT]
  Buzzer = Piezo Speaker
  IR_Sensor = fc-51 [package=THT]
  R2 = Resistor [tolerance=±5% resistance=220 package=THT]
  LED1 = LED - 5mm [color="Red (633nm)" package="5 mm [THT]"]
  U1 = ESP8266 NodeMCU LoLin base
  VCC1 = Battery block 9V  # not connected
  R3 = Resistor [tolerance=±5% resistance=220 package=THT]  # not connected

nets:
  N1: Emergency_Switch.leg0, Normal_Switch.leg0, Buzzer.pin1, IR_Sensor.pin2, LED1.cathode, U1.GND1-0, U1.GND1-1, U1.GND2-2, U1.GND3-2, U1.GND4
  N2: Emergency_Switch.leg1, R2.Pin_0, U1.D2-0, U1.D2-3
  N3: Normal_Switch.leg1, R1.Pin_1, U1.D1-0, U1.D1-3
  N4: R1.Pin_0, IR_Sensor.pin3, R2.Pin_1, U1.3V1-0, U1.3V2-3, U1.3V3-3
  N5: Buzzer.pin2, U1.D4-1, U1.D4-3
  N6: IR_Sensor.pin1, U1.D3-1, U1.D3-3
  N7: LED1.anode, U1.D5-0, U1.D5-3

notes:
  1 Normal Switch
  2 Emergency Switch
  3 IR
  4 Buzzer
  5 LED

custom parts:
  ESP8266 NodeMCU LoLin base: ESP8266 based NodeMCU Base
